// Logisim project DD1_Proj_2.circ as structural Verilog: 6 circuits, main circuit Left Shift Register
module main (
  input  [7:0] in_1,
  input  [7:0] in_2
);

  wire Clkout, EA, LA, left_shift_register_1_out;
  wire [7:0] multiplexer_1_out, n8bit_2_s_complementor_1_output;

  _8bit_2_s_Complementor u_8bit_2_s_complementor_1 (
    .Output(n8bit_2_s_complementor_1_output), .Input(in_1));  // open: out_3
  Multiplexer #(.width(8), .enable("false")) multiplexer_1 (
    .in0(in_1), .in1(n8bit_2_s_complementor_1_output), .out(multiplexer_1_out), .sel(in_1[7]));
  Left_Shift_Register left_shift_register_1 (
    .Load(LA), .Clk(Clkout), .Out(left_shift_register_1_out), .EN(EA), .D7(multiplexer_1_out[7]),
    .D6(multiplexer_1_out[6]), .D5(multiplexer_1_out[5]), .D4(multiplexer_1_out[4]),
    .D3(multiplexer_1_out[3]), .D2(multiplexer_1_out[2]), .D1(multiplexer_1_out[1]),
    .D0(multiplexer_1_out[0]), .Input(1'b0), .D14(1'b0), .D12(1'b0), .D10(1'b0), .D8(1'b0), .D15(1'b0),
    .D13(1'b0), .D11(1'b0), .D9(1'b0));
  Adder #(.width(1)) adder_1 (.a(left_shift_register_1_out), .cin(1'b0));  // open: b, out, cout
  _8bit_2_s_Complementor u_8bit_2_s_complementor_2 ();  // open: Output, Input, out_3
  _16bit_2_s_Complementor u_16bit_2_s_complementor_1 ();  // open: Input, Output
endmodule

// LSR
module Left_Shift_Register (
  input  Load,
  input  Clk,
  input  D14,
  input  D12,
  input  D10,
  input  D8,
  input  D6,
  input  D4,
  input  D2,
  input  D0,
  input  Input,
  input  D15,
  input  D13,
  input  D11,
  input  D9,
  input  D7,
  input  D5,
  input  D3,
  input  D1,
  input  EN,
  output Out
);

  wire d_ff_2_q, d_ff_3_q, d_ff_4_q, d_ff_5_q, d_ff_6_q, d_ff_7_q, d_ff_8_q, d_ff_9_q, d_ff_10_q, d_ff_11_q,
       d_ff_12_q, d_ff_13_q, d_ff_14_q, d_ff_15_q, d_ff_16_q, multiplexer_1_out, multiplexer_2_out,
       multiplexer_3_out, multiplexer_4_out, multiplexer_5_out, multiplexer_6_out, multiplexer_7_out,
       multiplexer_8_out, multiplexer_9_out, multiplexer_10_out, multiplexer_11_out, multiplexer_12_out,
       multiplexer_13_out, multiplexer_14_out, multiplexer_15_out, multiplexer_16_out;

  Multiplexer #(.enable("false")) multiplexer_1 (.in0(d_ff_2_q), .in1(D15), .out(multiplexer_1_out), .sel(Load));
  D_Flip_Flop #(.trigger("high")) d_ff_1 (
    .clk(Clk), .D(multiplexer_1_out), .Q(Out), .en(EN));  // open: Qn, preset, reset
  Multiplexer #(.enable("false")) multiplexer_2 (.in0(d_ff_3_q), .in1(D14), .out(multiplexer_2_out), .sel(Load));
  D_Flip_Flop #(.trigger("high")) d_ff_2 (
    .clk(Clk), .D(multiplexer_2_out), .Q(d_ff_2_q), .en(EN));  // open: Qn, preset, reset
  Multiplexer #(.enable("false")) multiplexer_3 (.in0(d_ff_4_q), .in1(D13), .out(multiplexer_3_out), .sel(Load));
  D_Flip_Flop #(.trigger("high")) d_ff_3 (
    .clk(Clk), .D(multiplexer_3_out), .Q(d_ff_3_q), .en(EN));  // open: Qn, preset, reset
  Multiplexer #(.enable("false")) multiplexer_4 (.in0(d_ff_5_q), .in1(D12), .out(multiplexer_4_out), .sel(Load));
  D_Flip_Flop #(.trigger("high")) d_ff_4 (
    .clk(Clk), .D(multiplexer_4_out), .Q(d_ff_4_q), .en(EN));  // open: Qn, preset, reset
  Multiplexer #(.enable("false")) multiplexer_5 (.in0(d_ff_6_q), .in1(D11), .out(multiplexer_5_out), .sel(Load));
  D_Flip_Flop #(.trigger("high")) d_ff_5 (
    .clk(Clk), .D(multiplexer_5_out), .Q(d_ff_5_q), .en(EN));  // open: Qn, preset, reset
  Multiplexer #(.enable("false")) multiplexer_6 (.in0(d_ff_7_q), .in1(D10), .out(multiplexer_6_out), .sel(Load));
  D_Flip_Flop #(.trigger("high")) d_ff_6 (
    .clk(Clk), .D(multiplexer_6_out), .Q(d_ff_6_q), .en(EN));  // open: Qn, preset, reset
  Multiplexer #(.enable("false")) multiplexer_7 (.in0(d_ff_8_q), .in1(D9), .out(multiplexer_7_out), .sel(Load));
  D_Flip_Flop #(.trigger("high")) d_ff_7 (
    .clk(Clk), .D(multiplexer_7_out), .Q(d_ff_7_q), .en(EN));  // open: Qn, preset, reset
  Multiplexer #(.enable("false")) multiplexer_8 (.in0(d_ff_9_q), .in1(D8), .out(multiplexer_8_out), .sel(Load));
  D_Flip_Flop #(.trigger("high")) d_ff_8 (
    .clk(Clk), .D(multiplexer_8_out), .Q(d_ff_8_q), .en(EN));  // open: Qn, preset, reset
  Multiplexer #(.enable("false")) multiplexer_9 (.in0(d_ff_10_q), .in1(D7), .out(multiplexer_9_out), .sel(Load));
  D_Flip_Flop #(.trigger("high")) d_ff_9 (
    .clk(Clk), .D(multiplexer_9_out), .Q(d_ff_9_q), .en(EN));  // open: Qn, preset, reset
  Multiplexer #(.enable("false")) multiplexer_10 (.in0(d_ff_11_q), .in1(D6), .out(multiplexer_10_out), .sel(Load));
  D_Flip_Flop #(.trigger("high")) d_ff_10 (
    .clk(Clk), .D(multiplexer_10_out), .Q(d_ff_10_q), .en(EN));  // open: Qn, preset, reset
  Multiplexer #(.enable("false")) multiplexer_11 (.in0(d_ff_12_q), .in1(D5), .out(multiplexer_11_out), .sel(Load));
  D_Flip_Flop #(.trigger("high")) d_ff_11 (
    .clk(Clk), .D(multiplexer_11_out), .Q(d_ff_11_q), .en(EN));  // open: Qn, preset, reset
  Multiplexer #(.enable("false")) multiplexer_12 (.in0(d_ff_13_q), .in1(D4), .out(multiplexer_12_out), .sel(Load));
  D_Flip_Flop #(.trigger("high")) d_ff_12 (
    .clk(Clk), .D(multiplexer_12_out), .Q(d_ff_12_q), .en(EN));  // open: Qn, preset, reset
  Multiplexer #(.enable("false")) multiplexer_13 (.in0(d_ff_14_q), .in1(D3), .out(multiplexer_13_out), .sel(Load));
  D_Flip_Flop #(.trigger("high")) d_ff_13 (
    .clk(Clk), .D(multiplexer_13_out), .Q(d_ff_13_q), .en(EN));  // open: Qn, preset, reset
  Multiplexer #(.enable("false")) multiplexer_14 (.in0(d_ff_15_q), .in1(D2), .out(multiplexer_14_out), .sel(Load));
  D_Flip_Flop #(.trigger("high")) d_ff_14 (
    .clk(Clk), .D(multiplexer_14_out), .Q(d_ff_14_q), .en(EN));  // open: Qn, preset, reset
  Multiplexer #(.enable("false")) multiplexer_15 (.in0(d_ff_16_q), .in1(D1), .out(multiplexer_15_out), .sel(Load));
  D_Flip_Flop #(.trigger("high")) d_ff_15 (
    .clk(Clk), .D(multiplexer_15_out), .Q(d_ff_15_q), .en(EN));  // open: Qn, preset, reset
  Multiplexer #(.enable("false")) multiplexer_16 (.in0(Input), .in1(D0), .out(multiplexer_16_out), .sel(Load));
  D_Flip_Flop #(.trigger("high")) d_ff_16 (
    .clk(Clk), .D(multiplexer_16_out), .Q(d_ff_16_q), .en(EN));  // open: Qn, preset, reset

  // Other names for the same wires on the sheet: ClkT = Clk; LoadT = Load
endmodule

module Sequential_Multiplier (
  input  [7:0] in_1,
  output [7:0] out_2
);

  wire [15:0] n16bit_2_s_complementor_1_output, undriven;

  _8bit_2_s_Complementor u_8bit_2_s_complementor_1 (.Output(out_2), .Input(in_1));  // open: out_3
  _16bit_2_s_Complementor u_16bit_2_s_complementor_1 (.Input(undriven), .Output(n16bit_2_s_complementor_1_output));
endmodule

module _8bit_2_s_Complementor (
  input  [7:0] Input,
  output [7:0] Output,
  output out_3
);

  wire [7:0] not_1_out;

  assign not_1_out = ~Input;  // NOT_Gate not_1, 8 bits wide
  Adder adder_1 (.a(not_1_out), .b({8{1'b0}}), .out(Output), .cin(1'b1), .cout(out_3));
endmodule

module _16bit_2_s_Complementor (
  input  [15:0] Input,
  output [15:0] Output
);

  wire [15:0] not_1_out;

  assign not_1_out = ~Input;  // NOT_Gate not_1, 16 bits wide
  Adder #(.width(16)) adder_1 (.a(not_1_out), .b({16{1'b0}}), .out(Output), .cin(1'b1));  // open: cout
endmodule

module LSR_8_bit (
  input  Load,
  input  Clk,
  input  D6,
  input  D4,
  input  D2,
  input  D0,
  input  Input,
  input  D7,
  input  D5,
  input  D3,
  input  D1,
  input  EN,
  output Out
);

  wire d_ff_2_q, d_ff_3_q, d_ff_4_q, d_ff_5_q, d_ff_6_q, d_ff_7_q, d_ff_8_q, multiplexer_1_out,
       multiplexer_2_out, multiplexer_3_out, multiplexer_4_out, multiplexer_5_out, multiplexer_6_out,
       multiplexer_7_out, multiplexer_8_out;

  Multiplexer #(.enable("false")) multiplexer_1 (.in0(d_ff_2_q), .in1(D7), .out(multiplexer_1_out), .sel(Load));
  D_Flip_Flop #(.trigger("high")) d_ff_1 (
    .clk(Clk), .D(multiplexer_1_out), .Q(Out), .en(EN));  // open: Qn, preset, reset
  Multiplexer #(.enable("false")) multiplexer_2 (.in0(d_ff_3_q), .in1(D6), .out(multiplexer_2_out), .sel(Load));
  D_Flip_Flop #(.trigger("high")) d_ff_2 (
    .clk(Clk), .D(multiplexer_2_out), .Q(d_ff_2_q), .en(EN));  // open: Qn, preset, reset
  Multiplexer #(.enable("false")) multiplexer_3 (.in0(d_ff_4_q), .in1(D5), .out(multiplexer_3_out), .sel(Load));
  D_Flip_Flop #(.trigger("high")) d_ff_3 (
    .clk(Clk), .D(multiplexer_3_out), .Q(d_ff_3_q), .en(EN));  // open: Qn, preset, reset
  Multiplexer #(.enable("false")) multiplexer_4 (.in0(d_ff_5_q), .in1(D4), .out(multiplexer_4_out), .sel(Load));
  D_Flip_Flop #(.trigger("high")) d_ff_4 (
    .clk(Clk), .D(multiplexer_4_out), .Q(d_ff_4_q), .en(EN));  // open: Qn, preset, reset
  Multiplexer #(.enable("false")) multiplexer_5 (.in0(d_ff_6_q), .in1(D3), .out(multiplexer_5_out), .sel(Load));
  D_Flip_Flop #(.trigger("high")) d_ff_5 (
    .clk(Clk), .D(multiplexer_5_out), .Q(d_ff_5_q), .en(EN));  // open: Qn, preset, reset
  Multiplexer #(.enable("false")) multiplexer_6 (.in0(d_ff_7_q), .in1(D2), .out(multiplexer_6_out), .sel(Load));
  D_Flip_Flop #(.trigger("high")) d_ff_6 (
    .clk(Clk), .D(multiplexer_6_out), .Q(d_ff_6_q), .en(EN));  // open: Qn, preset, reset
  Multiplexer #(.enable("false")) multiplexer_7 (.in0(d_ff_8_q), .in1(D1), .out(multiplexer_7_out), .sel(Load));
  D_Flip_Flop #(.trigger("high")) d_ff_7 (
    .clk(Clk), .D(multiplexer_7_out), .Q(d_ff_7_q), .en(EN));  // open: Qn, preset, reset
  Multiplexer #(.enable("false")) multiplexer_8 (.in0(Input), .in1(D0), .out(multiplexer_8_out), .sel(Load));
  D_Flip_Flop #(.trigger("high")) d_ff_8 (
    .clk(Clk), .D(multiplexer_8_out), .Q(d_ff_8_q), .en(EN));  // open: Qn, preset, reset

  // Other names for the same wires on the sheet: ClkT = Clk; LoadT = Load
endmodule
